# Fritzing sketch pcb (saved by Fritzing 0.9.3b)
circuit board: 8.46667cm x 5.64444cm
breadboards: 1

parts:
  botP = Pushbutton [package="[THT]"]
  C100µF = Electrolytic Capacitor [capacitance=100µF voltage=16V package="100 mil [THT, electrolytic]"]
  A4988 = Pololu A4988 [package=SO16]
  FCrec = Toggle Switch [package=THT]
  FCinj = Toggle Switch [package=THT]
  Part1 = Arduino Uno (Rev3)
  botIn = Pushbutton [package="[THT]"]
  Buzzer = Piezo Speaker
  LM317 = Voltage Regulator [part_number=LM package=to220-adj]
  R68Ω = Resistor [tolerance=±5% resistance=68 package=THT]
  R220 = Resistor [tolerance=±5% resistance=220 package=THT]
  Rb1 = Resistor [tolerance=±5% resistance=10k package=THT]
  Rb2 = Resistor [tolerance=±5% resistance=10k package=THT]
  Rb3 = Resistor [tolerance=±5% resistance=10k package=THT]
  Rb4 = Resistor [tolerance=±5% resistance=10k package=THT]
  LED1 = RGB LED (com. cathode, rgb) [package="5 mm [THT]"]
  Rlb = Resistor [tolerance=±5% resistance=100 package=THT]
  Rlg = Resistor [tolerance=±5% resistance=100 package=THT]
  Rlr = Resistor [tolerance=±5% resistance=100 package=THT]
  botM = Pushbutton [package="[THT]"]
  Rb5 = Resistor [tolerance=±5% resistance=10k package=THT]
  J1 = Power Jack [package=power_jack_combo]  # not connected
  BT1 = Bluetooth HC-06d [package=THT]
  Rhc06-01 = Resistor [tolerance=±5% resistance=330 package=THT]
  Rhc06-2 = Resistor [tolerance=±5% resistance=330 package=THT]
  Rhc06-3 = Resistor [tolerance=±5% resistance=330 package=THT]
  Grove1 = Grove OLED 128x96
  J2 = Basic Force Sensing Resistor (FSR) [package=THT]
  Nema14 = Stepper Motor - Bipolar

nets:
  N1: botP.Pin_1, botP.Pin_2, Rb1.Pin_1, Rb2.Pin_0
  VDD: botP.Pin_3, botP.Pin_4, A4988.VDD, FCrec.L2, FCinj.L2, Part1.3V3, botIn.Pin_3, botIn.Pin_4, botM.Pin_3, botM.Pin_4
  N2: C100µF.-, A4988.GND#14, LM317.ADJ, R68Ω.Pin_0
  N3: C100µF.+, A4988.VMOT, LM317.OUT
  N4: A4988.ENABLE, Part1.D5_PWM
  N5: A4988.RESET, A4988.SLEEP
  N6: A4988.STEP, Part1.D4
  N7: A4988.DIR, Part1.D3_PWM
  GND: A4988.GND#8, Part1.GND, Buzzer.pin1, Rb5.Pin_1, BT1.GND, Grove1.GND, J2.pin_1
  N8: A4988.1B, Nema14.B
  N9: A4988.1A, Nema14.C
  N10: A4988.2A, Nema14.A
  N11: A4988.2B, Nema14.D
  N12: FCrec.COM, Rb3.Pin_1, Rb4.Pin_0
  N13: FCinj.COM, Rb2.Pin_1, Rb3.Pin_0
  N14: Part1.A0, Rb4.Pin_1, botM.Pin_1, botM.Pin_2, Rb5.Pin_0
  N15: Part1.A1, J2.pin_0
  N16: Part1.A4/SDA, Grove1.SDA
  N17: Part1.A5/SCL, Grove1.SCL
  N18: Part1.D9_PWM, Rlr.Pin_0
  N19: Part1.D10_PWM/SS, Rlg.Pin_0
  N20: Part1.D12/MISO, Buzzer.pin2
  N21: Part1.D0/RX, BT1.TXD
  N22: Part1.D1/TX, BT1.RXD, Rhc06-01.Pin_0, Rhc06-01.Pin_1, Rhc06-2.Pin_0, Rhc06-2.Pin_1, Rhc06-3.Pin_0, Rhc06-3.Pin_1
  VCC: Part1.5V, BT1.VCC, Grove1.VCC
  N23: botIn.Pin_1, botIn.Pin_2, Rb1.Pin_0
  N24: LM317.IN, R68Ω.Pin_1, R220.Pin_0
  N25: LED1.red_anode, Rlr.Pin_1
  N26: LED1.green_anode, Rlg.Pin_1
  N27: LED1.blue_anode, Rlb.Pin_1

notes:
  Fonte 12V 1A
  capacitor eletrolitico 100uF
  Negativo plug
  5V
  miNUTRE
  Nutritech

custom parts:
  Bluetooth HC-06d: Bluetooth HC-06 - face down, pins down 16.5mm x 37.5mm PCB

// code stored in the sketch: Untitled3.ino

