# Fritzing sketch maquinaInjetora (saved by Fritzing 0.9.3b)
circuit board: 8.46667cm x 5.64444cm
breadboards: 1

parts:
  botRec = Pushbutton [package="[THT]"]
  C1 = Electrolytic Capacitor [capacitance=100µF voltage=16V package="100 mil [THT, electrolytic]"]
  RFimRecol = Resistor [tolerance=±5% resistance=100 package=THT]
  RfimInje = Resistor [tolerance=±5% resistance=100 package=THT]
  RbotRec = Resistor [tolerance=±5% resistance=100 package=THT]
  Part1 = Arduino Mega 2560 (Rev3)
  fimCursoRecolhimentoCompleto = Toggle Switch [package=THT]
  botIni = Momentary Switch [package=ksa_sealed_tac_switch]
  fimCursoInjecaoCompleto = Toggle Switch [package=THT]
  RbotInj = Resistor [tolerance=±5% resistance=100 package=THT]
  Nema14 = Stepper Motor - Bipolar
  driver = Pololu A4988 [package=SO16]
  botPa = Pushbutton [package="[THT]"]
  RbotPa = Resistor [tolerance=±5% resistance=100 package=THT]
  ledVermelho = LED - 3mm [color="Red (633nm)" package="3 mm [THT]"]
  RLver = Resistor [tolerance=±5% resistance=100 package=THT]
  ledVerde = LED - 5mm [color="Green (570nm)" package="5 mm [THT]"]
  R3lVer = Resistor [tolerance=±5% resistance=100 package=THT]
  Buzzer = Piezo Speaker

nets (from the breadboard view):
  N1: botRec.Pin_1, botRec.Pin_2, RbotRec.Pin_0, Part1.D10_PWM
  3V3: botRec.Pin_3, botRec.Pin_4, Part1.3V3, fimCursoRecolhimentoCompleto.L2, botIni.4, fimCursoInjecaoCompleto.L2, driver.VDD, botPa.Pin_3, botPa.Pin_4
  N2: C1.-, driver.GND#14
  N3: C1.+, driver.VMOT
  N4: RFimRecol.Pin_0, Part1.D8_PWM, fimCursoRecolhimentoCompleto.COM
  N5: RFimRecol.Pin_1, RbotRec.Pin_1, Part1.GND, Part1.D6_PWM, RbotInj.Pin_1, driver.GND#8, botPa.Pin_1, botPa.Pin_2, RbotPa.Pin_0, RbotPa.Pin_1, ledVermelho.cathode, ledVerde.cathode, Buzzer.pin1
  N6: RfimInje.Pin_0, Part1.D9_PWM, fimCursoInjecaoCompleto.COM
  N7: Part1.D13_PWM, ledVerde.anode, R3lVer.Pin_0, R3lVer.Pin_1
  N8: Part1.D12_PWM, Buzzer.pin2
  N9: Part1.D11_PWM, botIni.2, RbotInj.Pin_0
  N10: Part1.D3_PWM, driver.DIR
  N11: Part1.D4_PWM, driver.STEP
  N12: Part1.D5_PWM, driver.ENABLE
  N13: Part1.D7_PWM, ledVermelho.anode, RLver.Pin_0, RLver.Pin_1
  N14: Nema14.A, driver.2A
  N15: Nema14.C, driver.1A
  N16: Nema14.B, driver.1B
  N17: Nema14.D, driver.2B
  N18: driver.RESET, driver.SLEEP

notes:
  Fonte 12V 1A
  capacitor eletrolitico 100uF
